// Logisim project reloj_12hs.circ as structural Verilog: 8 circuits, main circuit main
module main (
  input  ena,
  input  rst,
  input  in_3,
  input  in_4,
  input  in_5,
  input  in_6
);

  wire and_1_out, and_2_out, and_3_out, and_4_out, and_5_out, clk_out, d0_1_a, d0_1_b, d0_1_c, d0_1_d,
       d0_1_f_9, d1_1_f_5, d1_1_qa, d1_1_qb, d1_1_qc, d3_1_a0, d3_1_a1, d3_1_a2, d3_1_a3, d3_1_f_9, d4_1_a0,
       decosiete_1_fa, decosiete_1_fb, decosiete_1_fc, decosiete_1_fd, decosiete_1_fe, decosiete_1_ff,
       decosiete_1_fg, decosiete_2_fa, decosiete_2_fb, decosiete_2_fc, decosiete_2_fd, decosiete_2_fe,
       decosiete_2_ff, decosiete_2_fg, decosiete_3_fa, decosiete_3_fb, decosiete_3_fc, decosiete_3_fd,
       decosiete_3_fe, decosiete_3_ff, decosiete_3_fg, decosiete_4_fa, decosiete_4_fb, decosiete_4_fc,
       decosiete_4_fd, decosiete_4_fe, decosiete_4_ff, decosiete_4_fg, not_1_out, not_2_out, not_3_out,
       or_1_out, or_2_out, or_3_out, or_4_out;

  Clock clk (.out(clk_out));
  or or_1 (or_1_out, rst, and_3_out);
  or or_2 (or_2_out, rst, and_3_out);
  and and_1 (and_1_out, d0_1_f_9, ena);
  and and_2 (and_2_out, d1_1_f_5, d0_1_f_9);
  and and_3 (and_3_out, and_5_out, d4_1_a0);
  and and_4 (and_4_out, or_3_out, d0_1_f_9, d1_1_f_5);
  and and_5 (and_5_out, not_1_out, d3_1_a1, not_3_out, not_2_out);
  or or_3 (or_3_out, and_3_out, d3_1_f_9);
  or or_4 (or_4_out, and_3_out, and_4_out);
  not not_1 (not_1_out, d3_1_a0);
  not not_2 (not_2_out, d3_1_a3);
  D0 d0_1 (.ena(ena), .clk(clk_out), .rst(rst), .A(d0_1_a), .B(d0_1_b), .f_9(d0_1_f_9), .C(d0_1_c), .D(d0_1_d));
  D1 d1_1 (.ena(and_1_out), .clk(clk_out), .rst(rst), .QA(d1_1_qa), .QB(d1_1_qb), .QC(d1_1_qc), .f_5(d1_1_f_5));
  D3 d3_1 (
    .ena(and_2_out), .clk(clk_out), .rst(or_1_out), .A0(d3_1_a0), .A3(d3_1_a3), .A2(d3_1_a2), .A1(d3_1_a1),
    .f_9(d3_1_f_9));
  not not_3 (not_3_out, d3_1_a2);
  D4 d4_1 (.ena(or_4_out), .clk(clk_out), .rst(or_2_out), .A0(d4_1_a0));
  DecoSiete decosiete_1 (
    .A3(d0_1_a), .A2(d0_1_b), .A1(d0_1_c), .A0(d0_1_d), .FA(decosiete_1_fa), .FB(decosiete_1_fb),
    .FC(decosiete_1_fc), .FD(decosiete_1_fd), .FE(decosiete_1_fe), .FF(decosiete_1_ff), .FG(decosiete_1_fg));
  DecoSiete decosiete_2 (
    .A3(in_3), .A2(d1_1_qa), .A1(d1_1_qb), .A0(d1_1_qc), .FA(decosiete_2_fa), .FB(decosiete_2_fb),
    .FC(decosiete_2_fc), .FD(decosiete_2_fd), .FE(decosiete_2_fe), .FF(decosiete_2_ff), .FG(decosiete_2_fg));
  DecoSiete decosiete_3 (
    .A3(d3_1_a3), .A2(d3_1_a2), .A1(d3_1_a1), .A0(d3_1_a0), .FA(decosiete_3_fa), .FB(decosiete_3_fb),
    .FC(decosiete_3_fc), .FD(decosiete_3_fd), .FE(decosiete_3_fe), .FF(decosiete_3_ff), .FG(decosiete_3_fg));
  DecoSiete decosiete_4 (
    .A3(in_4), .A2(in_5), .A1(in_6), .A0(d4_1_a0), .FA(decosiete_4_fa), .FB(decosiete_4_fb),
    .FC(decosiete_4_fc), .FD(decosiete_4_fd), .FE(decosiete_4_fe), .FF(decosiete_4_ff), .FG(decosiete_4_fg));
  _7_Segment_Display u_7_segment_display_1 (
    .g(decosiete_1_fg), .f(decosiete_1_ff), .a(decosiete_1_fa), .b(decosiete_1_fb), .e(decosiete_1_fe),
    .d(decosiete_1_fd), .c(decosiete_1_fc));  // open: dp
  _7_Segment_Display u_7_segment_display_2 (
    .g(decosiete_2_fg), .f(decosiete_2_ff), .a(decosiete_2_fa), .b(decosiete_2_fb), .e(decosiete_2_fe),
    .d(decosiete_2_fd), .c(decosiete_2_fc));  // open: dp
  _7_Segment_Display u_7_segment_display_3 (
    .g(decosiete_3_fg), .f(decosiete_3_ff), .a(decosiete_3_fa), .b(decosiete_3_fb), .e(decosiete_3_fe),
    .d(decosiete_3_fd), .c(decosiete_3_fc));  // open: dp
  _7_Segment_Display u_7_segment_display_4 (
    .g(decosiete_4_fg), .f(decosiete_4_ff), .a(decosiete_4_fa), .b(decosiete_4_fb), .e(decosiete_4_fe),
    .d(decosiete_4_fd), .c(decosiete_4_fc));  // open: dp
endmodule

module sieteSeg (
);

  wire decosiete_1_fa, decosiete_1_fb, decosiete_1_fc, decosiete_1_fd, decosiete_1_fe, decosiete_1_ff,
       decosiete_1_fg, dipswitch_1_p1, dipswitch_1_p2, dipswitch_1_p3, dipswitch_1_p4;

  // DipSwitch #(.number(4)) dipswitch_1: pin names not known; wires that end beside it: dipswitch_1_p1, dipswitch_1_p2, dipswitch_1_p3, dipswitch_1_p4
  DecoSiete decosiete_1 (
    .A3(dipswitch_1_p1), .A2(dipswitch_1_p2), .A1(dipswitch_1_p3), .A0(dipswitch_1_p4), .FA(decosiete_1_fa),
    .FB(decosiete_1_fb), .FC(decosiete_1_fc), .FD(decosiete_1_fd), .FE(decosiete_1_fe), .FF(decosiete_1_ff),
    .FG(decosiete_1_fg));
  _7_Segment_Display u_7_segment_display_1 (
    .g(decosiete_1_fg), .f(decosiete_1_ff), .a(decosiete_1_fa), .b(decosiete_1_fb), .e(decosiete_1_fe),
    .d(decosiete_1_fd), .c(decosiete_1_fc));  // open: dp
endmodule

module FFD_Enable (
  input  D,
  input  ena,
  input  clk,
  input  rst,
  output Q
);

  wire multiplexer_1_out;

  Multiplexer multiplexer_1 (.in0(Q), .in1(D), .out(multiplexer_1_out), .sel(ena));
  D_Flip_Flop d_ff_1 (.D(multiplexer_1_out), .clk(clk), .Q(Q), .reset(rst));  // open: Qn, preset
endmodule

module D0 (
  input  ena,
  input  clk,
  input  rst,
  output A,
  output B,
  output f_9,
  output C,
  output D
);

  wire and_1_out, and_2_out, and_3_out, and_4_out, and_5_out, and_6_out, and_7_out, not_1_out, not_2_out,
       not_3_out, not_4_out, not_5_out, not_6_out, or_1_out, or_2_out, or_3_out;

  and and_1 (and_1_out, C, B, D);
  and and_2 (and_2_out, not_2_out, not_3_out, A);
  and and_3 (and_3_out, not_3_out, C, B);
  and and_4 (and_4_out, not_1_out, D, C);
  and and_5 (and_5_out, B, not_2_out);
  and and_6 (and_6_out, C, not_3_out);
  and and_7 (and_7_out, D, not_2_out, not_4_out);
  or or_1 (or_1_out, and_1_out, and_2_out);
  or or_2 (or_2_out, and_3_out, and_4_out, and_5_out);
  or or_3 (or_3_out, and_6_out, and_7_out);
  FFD_Enable FFD_A (.D(or_1_out), .ena(ena), .clk(clk), .rst(rst), .Q(A));
  FFD_Enable FFD_B (.D(or_2_out), .ena(ena), .clk(clk), .rst(rst), .Q(B));
  FFD_Enable FFD_C (.D(or_3_out), .ena(ena), .clk(clk), .rst(rst), .Q(C));
  FFD_Enable FFD_D (.D(not_3_out), .ena(ena), .clk(clk), .rst(rst), .Q(D));
  not not_1 (not_1_out, B);
  not not_2 (not_2_out, C);
  not not_3 (not_3_out, D);
  not not_4 (not_4_out, A);
  LED led_1 (.in(A));
  LED led_2 (.in(B));
  LED led_3 (.in(C));
  LED led_4 (.in(D));
  not not_5 (not_5_out, B);
  not not_6 (not_6_out, C);
  and and_8 (f_9, A, not_5_out, not_6_out, D);
endmodule

module DecoSiete (
  input  A3,
  input  A2,
  input  A1,
  input  A0,
  output FA,
  output FB,
  output FC,
  output FD,
  output FE,
  output FF,
  output FG
);

  wire and_1_out, and_2_out, and_3_out, and_4_out, and_5_out, and_6_out, and_7_out, and_8_out, and_9_out,
       and_10_out, and_11_out, and_12_out, and_13_out, and_14_out, and_15_out, and_16_out, and_17_out,
       and_18_out, and_19_out, and_20_out, not_1_out, not_2_out, not_3_out, not_4_out;

  not not_1 (not_1_out, A3);
  not not_2 (not_2_out, A2);
  not not_3 (not_3_out, A1);
  not not_4 (not_4_out, A0);
  and and_1 (and_1_out, A2, A0);
  and and_2 (and_2_out, not_4_out, not_2_out);
  and and_3 (and_3_out, A0, A1);
  and and_4 (and_4_out, not_4_out, not_3_out);
  and and_5 (and_5_out, not_4_out, not_3_out);
  and and_6 (and_6_out, not_2_out, not_4_out);
  and and_7 (and_7_out, A0, not_3_out, A2);
  and and_8 (and_8_out, A1, not_2_out);
  and and_9 (and_9_out, not_4_out, A1);
  and and_10 (and_10_out, not_3_out, A3);
  and and_11 (and_11_out, not_4_out, not_2_out);
  and and_12 (and_12_out, not_4_out, A1);
  and and_13 (and_13_out, A3, not_2_out);
  and and_14 (and_14_out, A2, not_3_out);
  and and_15 (and_15_out, A2, not_4_out);
  and and_16 (and_16_out, not_4_out, not_3_out);
  and and_17 (and_17_out, A1, not_4_out);
  and and_18 (and_18_out, A2, not_3_out);
  and and_19 (and_19_out, A3, not_2_out);
  and and_20 (and_20_out, not_2_out, A1);
  or or_1 (FA, A1, A3, and_1_out, and_2_out);
  or or_2 (FB, not_2_out, and_3_out, and_4_out);
  or or_3 (FC, A0, A2, and_5_out);
  or or_4 (FD, and_6_out, and_7_out, and_10_out, and_8_out, and_9_out);
  or or_5 (FE, and_11_out, and_12_out);
  or or_6 (FF, and_13_out, and_14_out, and_15_out, and_16_out);
  or or_7 (FG, and_17_out, and_18_out, and_19_out, and_20_out);
endmodule

module D1 (
  input  ena,
  input  clk,
  input  rst,
  output QA,
  output QB,
  output QC,
  output f_5
);

  wire and_1_out, and_2_out, and_3_out, and_4_out, not_1_out, not_2_out, not_3_out, not_4_out, or_1_out,
       or_2_out;

  and and_1 (and_1_out, not_2_out, QA);
  and and_2 (and_2_out, QB, QC);
  and and_3 (and_3_out, QC, not_3_out, not_1_out);
  and and_4 (and_4_out, QB, not_2_out);
  or or_1 (or_1_out, and_1_out, and_2_out);
  or or_2 (or_2_out, and_3_out, and_4_out);
  FFD_Enable FFD_A (.D(or_1_out), .ena(ena), .clk(clk), .rst(rst), .Q(QA));
  FFD_Enable FFD_B (.D(or_2_out), .ena(ena), .clk(clk), .rst(rst), .Q(QB));
  FFD_Enable FFD_C (.D(not_2_out), .ena(ena), .clk(clk), .rst(rst), .Q(QC));
  not not_1 (not_1_out, QB);
  not not_2 (not_2_out, QC);
  not not_3 (not_3_out, QA);
  not not_4 (not_4_out, QB);
  and and_5 (f_5, QA, not_4_out, QC);
endmodule

module D3 (
  input  ena,
  input  clk,
  input  rst,
  output A0,
  output A3,
  output A2,
  output A1,
  output f_9
);

  wire and_1_out, and_2_out, and_3_out, and_5_out, not_1_out, not_2_out, not_3_out, not_4_out, or_1_out,
       or_2_out, or_3_out, xor_1_out, xor_2_out, xor_3_out, xor_4_out;

  or or_1 (or_1_out, and_3_out, rst);
  xor xor_1 (xor_1_out, and_1_out, A3);
  and and_1 (and_1_out, and_2_out, A2);
  FFD_Enable ffd_enable_1 (.D(xor_1_out), .ena(1'b1), .clk(clk), .rst(or_1_out), .Q(A3));
  or or_2 (or_2_out, and_3_out, rst);
  xor xor_2 (xor_2_out, and_2_out, A2);
  and and_2 (and_2_out, and_5_out, A1);
  FFD_Enable ffd_enable_2 (.D(xor_2_out), .ena(1'b1), .clk(clk), .rst(or_2_out), .Q(A2));
  not not_1 (not_1_out, A2);
  and and_3 (and_3_out, A3, not_1_out, A1, not_4_out);
  or or_3 (or_3_out, and_3_out, rst);
  xor xor_3 (xor_3_out, and_5_out, A1);
  not not_2 (not_2_out, A1);
  not not_3 (not_3_out, A2);
  and and_4 (f_9, A3, not_3_out, not_2_out, A0);
  and and_5 (and_5_out, ena, A0);
  FFD_Enable ffd_enable_3 (.D(xor_3_out), .ena(1'b1), .clk(clk), .rst(or_3_out), .Q(A1));
  not not_4 (not_4_out, A0);
  xor xor_4 (xor_4_out, ena, A0);
  FFD_Enable ffd_enable_4 (.D(xor_4_out), .ena(1'b1), .clk(clk), .rst(rst), .Q(A0));
endmodule

module D4 (
  input  ena,
  input  clk,
  input  rst,
  output A0
);

  wire not_1_out;

  not not_1 (not_1_out, A0);
  FFD_Enable ffd_enable_1 (.D(not_1_out), .ena(ena), .clk(clk), .rst(rst), .Q(A0));
endmodule
